# Fritzing sketch Dual-Vision-Shield-TB6612FNG-RevC (saved by Fritzing 1.0.6)
circuit board: 6.25cm x 3.55cm
breadboards: 1

parts:
  J3 = female pin header, 16 pins [form="♀ (female)"]  # not connected
  J1 = female pin header, 16 pins [form="♀ (female)"]
  J12 = female pin header, 8 pins [form="♀ (female)"]
  J11 = female pin header, 8 pins [form="♀ (female)"]
  J17 = Screw terminal - 2 pins [package=THT]
  R7 = Resistor [tolerance=±5% power=0.25W resistance=10k package=THT]
  J18 = male pin header, 4 pins [form="♂ (male)"]
  R8 = Resistor [tolerance=±5% power=0.25W resistance=4.7k package=THT]
  J19 = male pin header, 4 pins [form="♂ (male)"]
  R9 = Resistor [tolerance=±5% power=0.25W resistance=4.7k package=THT]
  C1 = Tantalum Capacitor [capacitance=22µF voltage=16V package="100 mil [THT, tantalum]"]
  J6 = male pin header, 7 pins [form="♂ (male)"]
  J5 = male pin header, 7 pins [form="♂ (male)"]
  J16 = male pin header, 3 pins [form="♂ (male)"]
  J16_2 = male pin header, 3 pins [form="♂ (male)"]
  J8 = male pin header, 5 pins [form="♂ (male)"]
  J13 = male pin header, 2 pins [form="♂ (male)"]
  J14 = male pin header, 2 pins [form="♂ (male)"]
  J8_2 = male pin header, 5 pins [form="♂ (male)"]

nets:
  N1: J1.pin1, J11.pin2, R7.Pin_1, J18.pin3, J19.pin3, J5.pin5, J16.pin3, J16_2.pin3
  N2: J1.pin2, J12.pin8, J11.pin3, J11.pin8, J17.pin1, J18.pin4, R8.Pin_1, J19.pin4, R9.Pin_1, C1.+, J5.pin6
  N3: J1.pin3, J6.pin3
  N4: J1.pin4, R9.Pin_0, J6.pin2
  N5: J1.pin7, J18.pin1
  N6: J1.pin8, J18.pin2, J19.pin1
  N7: J1.pin9, J12.pin1, J19.pin2
  N8: J1.pin10, J12.pin2
  N9: J1.pin11, J12.pin3
  N10: J1.pin12, J12.pin5
  N11: J1.pin13, J12.pin6
  N12: J1.pin14, J12.pin7
  N13: J1.pin16, J16.pin1, J16_2.pin1
  N14: J12.pin4, R7.Pin_0
  N15: J11.pin1, J17.pin2, C1.-, J16.pin2, J16_2.pin2
  N16: J11.pin4, J8.pin2, J13.pin1, J8_2.pin2
  N17: J11.pin5, J8.pin4, J13.pin2, J8_2.pin4
  N18: J11.pin6, J8.pin3, J14.pin1, J8_2.pin3
  N19: J11.pin7, J8.pin5, J14.pin2, J8_2.pin5

notes:
  GND
  3V3
  SCL
  SDA
  SM/DCM-VISION-I2C
  VISION-AI
  TB6612FNG
  B2
  A2
  A1
  VCC
  B1
  VMOT
  STBY
  AIN1
  AIN2
  BIN2
  BIN1
  PWMA
  PWMB
  1
  2
  EXT
  + -
  D3
  D4
  D5
  D6
  D7
  D0
  D1
  D2
  5V
  D
  A
  B
  C
  X
  +  -
  Rev. C
